# Fritzing sketch pcb_barwin (saved by Fritzing 0.9.3b)
circuit board: 7cm x 10cm

parts:
  J1 = male pin header, 6 pins [form="♂ (male)"]
  J2 = male pin header, 8 pins [form="♂ (male)"]
  J3 = male pin header, 8 pins [form="♂ (male)"]
  J4 = male pin header, 10 pins [form="♂ (male)"]
  J5 = Basic Servo  # not connected
  J7 = Basic Servo  # not connected
  J8 = Basic Servo  # not connected
  J9 = Basic Servo  # not connected
  servo1 = female pin header, 3 pins [form="♀ (female)"]
  J12 = Basic Servo  # not connected
  J13 = Basic Servo  # not connected
  servo3 = female pin header, 3 pins [form="♀ (female)"]
  servo6 = female pin header, 3 pins [form="♀ (female)"]
  servo4 = female pin header, 3 pins [form="♀ (female)"]
  J6 = Basic Servo  # not connected
  servo0 = female pin header, 3 pins [form="♀ (female)"]
  Part1 = Arduino Uno (Rev3)  # not connected
  J20 = female pin header, 4 pins [form="♀ (female)"]
  servo5 = female pin header, 3 pins [form="♀ (female)"]
  Input_5V = female pin header, 2 pins [form="♀ (female)"]
  Input_12V = female pin header, 2 pins [form="♀ (female)"]
  Input_5V1 = female pin header, 2 pins [form="♀ (female)"]
  Input_12V1 = female pin header, 2 pins [form="♀ (female)"]
  servo_off = female pin header, 2 pins [form="♀ (female)"]
  buttons = female pin header, 8 pins [form="♀ (female)"]
  servo2 = female pin header, 3 pins [form="♀ (female)"]

nets:
  N1: J1.pin1, J20.pin2
  N2: J1.pin2, J20.pin3
  N3: J1.pin3, buttons.pin5
  N4: J1.pin4, buttons.pin6
  N5: J1.pin5, buttons.pin7
  N6: J1.pin6, buttons.pin8
  N7: J2.pin8, J20.pin4, Input_12V.pin2, Input_12V1.pin2
  N8: J3.pin2, servo2.pin3
  N9: J3.pin3, servo1.pin3
  N10: J3.pin4, buttons.pin4
  N11: J3.pin5, servo0.pin3
  N12: J3.pin6, buttons.pin3
  N13: J3.pin7, buttons.pin2
  N14: J3.pin8, buttons.pin1
  N15: J4.pin4, servo1.pin1, servo3.pin1, servo6.pin1, servo4.pin1, servo0.pin1, J20.pin1, servo5.pin1, Input_5V.pin1, Input_12V.pin1, Input_5V1.pin1, Input_12V1.pin1, servo2.pin1
  N16: J4.pin5, servo6.pin3
  N17: J4.pin7, servo5.pin3
  N18: J4.pin8, servo4.pin3
  N19: J4.pin9, servo3.pin3
  N20: servo1.pin2, servo3.pin2, servo6.pin2, servo4.pin2, servo0.pin2, servo5.pin2, servo_off.pin1, servo2.pin2
  N21: Input_5V.pin2, Input_5V1.pin2, servo_off.pin2

notes:
  GND
  IN 12V
  servo_off
  IN 5V
  servos
